// Logisim project 16 Bit ALU_Indirect_Addressing_Mode_CA.circ as structural Verilog: 3 circuits, main circuit main
module main (
  input  [15:0] in_1,
  input  [15:0] in_2,
  output Error
);

  wire _0, _1, _2, _3, button_1_out, button_2_out, button_3_out, button_4_out, button_5_out, button_6_out,
       button_7_out, button_8_out, clock_1_out, clock_2_out, controlled_buffer_4_out,
       controlled_buffer_5_out, n7_segment_display_1_a_2, n7_segment_display_1_b_2, n7_segment_display_1_c_2,
       n7_segment_display_1_d_2, n7_segment_display_1_e, n7_segment_display_1_f, n7_segment_display_1_g,
       n7_segment_display_3_a_2, n7_segment_display_3_b_2, n7_segment_display_3_c_2,
       n7_segment_display_3_d_2, n7_segment_display_3_e, n7_segment_display_3_f, n7_segment_display_3_g,
       n7_segment_display_5_a_2, n7_segment_display_5_b_2, n7_segment_display_5_c_2,
       n7_segment_display_5_d_2, n7_segment_display_5_e, n7_segment_display_5_f, n7_segment_display_5_g,
       n7_segment_display_7_a_2, n7_segment_display_7_b_2, n7_segment_display_7_c_2,
       n7_segment_display_7_d_2, n7_segment_display_7_e, n7_segment_display_7_f, n7_segment_display_7_g,
       n7_segment_display_9_a_2, n7_segment_display_9_b_2, n7_segment_display_9_c_2,
       n7_segment_display_9_d_2, n7_segment_display_9_e, n7_segment_display_9_f, n7_segment_display_9_g,
       n7_segment_display_11_a_2, n7_segment_display_11_b_2, n7_segment_display_11_c_2,
       n7_segment_display_11_d_2, n7_segment_display_11_e, n7_segment_display_11_f, n7_segment_display_11_g,
       n7_segment_display_13_a_2, n7_segment_display_13_b_2, n7_segment_display_13_c_2,
       n7_segment_display_13_d_2, n7_segment_display_13_e, n7_segment_display_13_f, n7_segment_display_13_g,
       n7_segment_display_15_a_2, n7_segment_display_15_b_2, n7_segment_display_15_c_2,
       n7_segment_display_15_d_2, n7_segment_display_15_e, n7_segment_display_15_f, n7_segment_display_15_g,
       n7_segment_display_17_a_2, n7_segment_display_17_b_2, n7_segment_display_17_c_2,
       n7_segment_display_17_d_2, n7_segment_display_17_e, n7_segment_display_17_f, n7_segment_display_17_g,
       n7_segment_display_19_a_2, n7_segment_display_19_b_2, n7_segment_display_19_c_2,
       n7_segment_display_19_d_2, n7_segment_display_19_e, n7_segment_display_19_f, n7_segment_display_19_g,
       or_1_out;
  wire [1:0] counter_1_q;
  wire [2:0] priority_encoder_1_out, register_1_q;
  wire [2:2] not_1_out;
  wire [3:0] divider_1_out, divider_1_out_2, divider_1_out_3, divider_1_out_4, divider_1_out_5,
       divider_1_out_6, divider_1_out_7, divider_1_out_8, divider_4_rem, divider_4_rem_2, divider_4_rem_3,
       divider_4_rem_4, divider_4_rem_5, divider_4_rem_6, divider_4_rem_7, divider_4_rem_8;
  wire [4:4] alu_1_output_2;
  wire [15:0] controlled_buffer_1_out, controlled_buffer_3_out, controlled_buffer_6_out, ram_1_data,
       register_2_q;
  wire [30:0] alu_1_output;
  wire [31:0] adder_1_out, divider_1_rem, divider_2_out, divider_2_rem, divider_3_out, divider_3_rem,
       divider_4_out, divider_5_out, divider_5_rem, divider_6_out, divider_6_rem, divider_7_out,
       divider_7_rem, divider_8_out, divider_8_rem, divider_9_out, divider_9_rem, multiplexer_1_out,
       not_2_out;

  not not_1 (not_1_out[2], alu_1_output_2[4]);
  Button button_1 (.out(button_1_out));
  Button button_2 (.out(button_2_out));
  Button button_3 (.out(button_3_out));
  Button button_4 (.out(button_4_out));
  Button button_5 (.out(button_5_out));
  Button button_6 (.out(button_6_out));
  Button button_7 (.out(button_7_out));
  Button button_8 (.out(button_8_out));
  assign controlled_buffer_1_out = _0 ? in_2 : 16'bz;  // Controlled_Buffer controlled_buffer_1
  DotMatrix #(.inputtype("row"), .matrixrows(5)) dotmatrix_1 (
    .row0({5{1'b0}}), .row1({2'b00, not_1_out[2], 2'b00}),
    .row2({alu_1_output_2[4], 3'b111, alu_1_output_2[4]}), .row3({2'b00, not_1_out[2], 2'b00}),
    .row4({5{1'b0}}));
  // Probe on in_1
  // Probe on register_2_q
  assign controlled_buffer_1_out = _2 ? controlled_buffer_3_out : 16'bz;  // Controlled_Buffer controlled_buffer_2
  assign controlled_buffer_3_out = _1 ? ram_1_data : 16'bz;  // Controlled_Buffer controlled_buffer_3
  _7_Segment_Display u_7_segment_display_1 (
    .D(divider_1_out[3]), .C(divider_1_out[2]), .B(divider_1_out[1]), .A(divider_1_out[0]),
    .a_2(n7_segment_display_1_a_2), .b_2(n7_segment_display_1_b_2), .c_2(n7_segment_display_1_c_2),
    .d_2(n7_segment_display_1_d_2), .e(n7_segment_display_1_e), .f(n7_segment_display_1_f),
    .g(n7_segment_display_1_g));
  _7_Segment_Display_part u_7_segment_display_2 (
    .g(n7_segment_display_1_g), .f(n7_segment_display_1_f), .a(n7_segment_display_1_a_2),
    .b(n7_segment_display_1_b_2), .e(n7_segment_display_1_e), .d(n7_segment_display_1_d_2),
    .c(n7_segment_display_1_c_2));  // open: dp
  or or_1 (or_1_out, button_1_out, button_2_out, button_3_out, button_4_out, button_5_out, button_6_out, button_7_out, button_8_out);
  Divider #(.width(32)) divider_1 (
    .a(divider_2_out), .b(32'ha),
    .out({divider_1_out_8, divider_1_out_7, divider_1_out_6, divider_1_out_5, divider_1_out_4, divider_1_out_3, divider_1_out_2, divider_1_out}),
    .rem(divider_1_rem));  // open: upper
  Priority_Encoder priority_encoder_1 (
    .in0(button_1_out), .in1(button_2_out), .in2(button_3_out), .in3(button_4_out), .in4(button_5_out),
    .in5(button_6_out), .in6(button_7_out), .in7(button_8_out), .out(priority_encoder_1_out));  // open: en_in, gs, en_out
  assign controlled_buffer_4_out = 1'b1 ? or_1_out : 1'bz;  // Controlled_Buffer controlled_buffer_4
  assign controlled_buffer_5_out = 1'b1 ? controlled_buffer_4_out : 1'bz;  // Controlled_Buffer controlled_buffer_5
  ALU alu_1 (.a(in_1), .b(register_2_q), .c(register_1_q), .Output({alu_1_output_2[4], alu_1_output}), .Error(Error));
  Clock clock_1 (.out(clock_1_out));
  _7_Segment_Display u_7_segment_display_3 (
    .D(divider_1_rem[3]), .C(divider_1_rem[2]), .B(divider_1_rem[1]), .A(divider_1_rem[0]),
    .a_2(n7_segment_display_3_a_2), .b_2(n7_segment_display_3_b_2), .c_2(n7_segment_display_3_c_2),
    .d_2(n7_segment_display_3_d_2), .e(n7_segment_display_3_e), .f(n7_segment_display_3_f),
    .g(n7_segment_display_3_g));
  Register #(.width(3)) register_1 (
    .D(priority_encoder_1_out), .en(controlled_buffer_5_out), .Q(register_1_q), .clk(controlled_buffer_5_out));  // open: clr
  RAM #(.addrWidth(16), .dataWidth(16)) ram_1 (
    .addr(controlled_buffer_1_out), .data(ram_1_data), .clk(clock_1_out));  // open: sel, ld, clr
  _7_Segment_Display_part u_7_segment_display_4 (
    .g(n7_segment_display_3_g), .f(n7_segment_display_3_f), .a(n7_segment_display_3_a_2),
    .b(n7_segment_display_3_b_2), .e(n7_segment_display_3_e), .d(n7_segment_display_3_d_2),
    .c(n7_segment_display_3_c_2));  // open: dp
  Divider #(.width(32)) divider_2 (
    .a(divider_3_out), .b(32'ha), .out(divider_2_out), .rem(divider_2_rem));  // open: upper
  assign not_2_out = ~{alu_1_output_2[4], alu_1_output};  // NOT_Gate not_2, 32 bits wide
  _7_Segment_Display u_7_segment_display_5 (
    .D(divider_2_rem[3]), .C(divider_2_rem[2]), .B(divider_2_rem[1]), .A(divider_2_rem[0]),
    .a_2(n7_segment_display_5_a_2), .b_2(n7_segment_display_5_b_2), .c_2(n7_segment_display_5_c_2),
    .d_2(n7_segment_display_5_d_2), .e(n7_segment_display_5_e), .f(n7_segment_display_5_f),
    .g(n7_segment_display_5_g));
  _7_Segment_Display_part u_7_segment_display_6 (
    .g(n7_segment_display_5_g), .f(n7_segment_display_5_f), .a(n7_segment_display_5_a_2),
    .b(n7_segment_display_5_b_2), .e(n7_segment_display_5_e), .d(n7_segment_display_5_d_2),
    .c(n7_segment_display_5_c_2));  // open: dp
  Divider #(.width(32)) divider_3 (
    .a(divider_4_out), .b(32'ha), .out(divider_3_out), .rem(divider_3_rem));  // open: upper
  Adder #(.width(32)) adder_1 (.a(not_2_out), .b(32'h1), .out(adder_1_out));  // open: cin, cout
  assign controlled_buffer_6_out = _3 ? ram_1_data : 16'bz;  // Controlled_Buffer controlled_buffer_6
  _7_Segment_Display u_7_segment_display_7 (
    .D(divider_3_rem[3]), .C(divider_3_rem[2]), .B(divider_3_rem[1]), .A(divider_3_rem[0]),
    .a_2(n7_segment_display_7_a_2), .b_2(n7_segment_display_7_b_2), .c_2(n7_segment_display_7_c_2),
    .d_2(n7_segment_display_7_d_2), .e(n7_segment_display_7_e), .f(n7_segment_display_7_f),
    .g(n7_segment_display_7_g));
  Multiplexer #(.width(32)) multiplexer_1 (
    .in0({alu_1_output_2[4], alu_1_output}), .in1(adder_1_out), .out(multiplexer_1_out),
    .sel(alu_1_output_2[4]));  // open: en
  Register #(.width(16)) register_2 (
    .D(controlled_buffer_6_out), .Q(register_2_q), .clk(clock_1_out));  // open: en, clr
  _7_Segment_Display_part u_7_segment_display_8 (
    .g(n7_segment_display_7_g), .f(n7_segment_display_7_f), .a(n7_segment_display_7_a_2),
    .b(n7_segment_display_7_b_2), .e(n7_segment_display_7_e), .d(n7_segment_display_7_d_2),
    .c(n7_segment_display_7_c_2));  // open: dp
  Divider #(.width(32)) divider_4 (
    .a(divider_5_out), .b(32'ha), .out(divider_4_out),
    .rem({divider_4_rem_8, divider_4_rem_7, divider_4_rem_6, divider_4_rem_5, divider_4_rem_4, divider_4_rem_3, divider_4_rem_2, divider_4_rem}));  // open: upper
  Clock clock_2 (.out(clock_2_out));
  Counter #(.width(2), .max('h3)) counter_1 (.Q(counter_1_q), .clk(clock_2_out));  // open: load, D, count, carry, clr
  _7_Segment_Display u_7_segment_display_9 (
    .D(divider_4_rem[3]), .C(divider_4_rem[2]), .B(divider_4_rem[1]), .A(divider_4_rem[0]),
    .a_2(n7_segment_display_9_a_2), .b_2(n7_segment_display_9_b_2), .c_2(n7_segment_display_9_c_2),
    .d_2(n7_segment_display_9_d_2), .e(n7_segment_display_9_e), .f(n7_segment_display_9_f),
    .g(n7_segment_display_9_g));
  _7_Segment_Display_part u_7_segment_display_10 (
    .g(n7_segment_display_9_g), .f(n7_segment_display_9_f), .a(n7_segment_display_9_a_2),
    .b(n7_segment_display_9_b_2), .e(n7_segment_display_9_e), .d(n7_segment_display_9_d_2),
    .c(n7_segment_display_9_c_2));  // open: dp
  Divider #(.width(32)) divider_5 (
    .a(divider_6_out), .b(32'ha), .out(divider_5_out), .rem(divider_5_rem));  // open: upper
  // Probe on {alu_1_output_2[4], alu_1_output}
  Comparator #(.width(2)) comparator_1 (.a(2'b00), .b(counter_1_q), .eq(_0));  // open: gt, lt
  Comparator #(.width(2)) comparator_2 (.a(2'b01), .b(counter_1_q), .eq(_1));  // open: gt, lt
  Comparator #(.width(2)) comparator_3 (.a(2'b10), .b(counter_1_q), .eq(_2));  // open: gt, lt
  Comparator #(.width(2)) comparator_4 (.a(2'b11), .b(counter_1_q), .eq(_3));  // open: gt, lt
  _7_Segment_Display u_7_segment_display_11 (
    .D(divider_5_rem[3]), .C(divider_5_rem[2]), .B(divider_5_rem[1]), .A(divider_5_rem[0]),
    .a_2(n7_segment_display_11_a_2), .b_2(n7_segment_display_11_b_2), .c_2(n7_segment_display_11_c_2),
    .d_2(n7_segment_display_11_d_2), .e(n7_segment_display_11_e), .f(n7_segment_display_11_f),
    .g(n7_segment_display_11_g));
  _7_Segment_Display_part u_7_segment_display_12 (
    .g(n7_segment_display_11_g), .f(n7_segment_display_11_f), .a(n7_segment_display_11_a_2),
    .b(n7_segment_display_11_b_2), .e(n7_segment_display_11_e), .d(n7_segment_display_11_d_2),
    .c(n7_segment_display_11_c_2));  // open: dp
  Divider #(.width(32)) divider_6 (
    .a(divider_7_out), .b(32'ha), .out(divider_6_out), .rem(divider_6_rem));  // open: upper
  _7_Segment_Display u_7_segment_display_13 (
    .D(divider_6_rem[3]), .C(divider_6_rem[2]), .B(divider_6_rem[1]), .A(divider_6_rem[0]),
    .a_2(n7_segment_display_13_a_2), .b_2(n7_segment_display_13_b_2), .c_2(n7_segment_display_13_c_2),
    .d_2(n7_segment_display_13_d_2), .e(n7_segment_display_13_e), .f(n7_segment_display_13_f),
    .g(n7_segment_display_13_g));
  _7_Segment_Display_part u_7_segment_display_14 (
    .g(n7_segment_display_13_g), .f(n7_segment_display_13_f), .a(n7_segment_display_13_a_2),
    .b(n7_segment_display_13_b_2), .e(n7_segment_display_13_e), .d(n7_segment_display_13_d_2),
    .c(n7_segment_display_13_c_2));  // open: dp
  Divider #(.width(32)) divider_7 (
    .a(divider_8_out), .b(32'ha), .out(divider_7_out), .rem(divider_7_rem));  // open: upper
  _7_Segment_Display u_7_segment_display_15 (
    .D(divider_7_rem[3]), .C(divider_7_rem[2]), .B(divider_7_rem[1]), .A(divider_7_rem[0]),
    .a_2(n7_segment_display_15_a_2), .b_2(n7_segment_display_15_b_2), .c_2(n7_segment_display_15_c_2),
    .d_2(n7_segment_display_15_d_2), .e(n7_segment_display_15_e), .f(n7_segment_display_15_f),
    .g(n7_segment_display_15_g));
  _7_Segment_Display_part u_7_segment_display_16 (
    .g(n7_segment_display_15_g), .f(n7_segment_display_15_f), .a(n7_segment_display_15_a_2),
    .b(n7_segment_display_15_b_2), .e(n7_segment_display_15_e), .d(n7_segment_display_15_d_2),
    .c(n7_segment_display_15_c_2));  // open: dp
  Divider #(.width(32)) divider_8 (
    .a(divider_9_out), .b(32'ha), .out(divider_8_out), .rem(divider_8_rem));  // open: upper
  _7_Segment_Display u_7_segment_display_17 (
    .D(divider_8_rem[3]), .C(divider_8_rem[2]), .B(divider_8_rem[1]), .A(divider_8_rem[0]),
    .a_2(n7_segment_display_17_a_2), .b_2(n7_segment_display_17_b_2), .c_2(n7_segment_display_17_c_2),
    .d_2(n7_segment_display_17_d_2), .e(n7_segment_display_17_e), .f(n7_segment_display_17_f),
    .g(n7_segment_display_17_g));
  _7_Segment_Display_part u_7_segment_display_18 (
    .g(n7_segment_display_17_g), .f(n7_segment_display_17_f), .a(n7_segment_display_17_a_2),
    .b(n7_segment_display_17_b_2), .e(n7_segment_display_17_e), .d(n7_segment_display_17_d_2),
    .c(n7_segment_display_17_c_2));  // open: dp
  Divider #(.width(32)) divider_9 (
    .a(multiplexer_1_out), .b(32'ha), .out(divider_9_out), .rem(divider_9_rem));  // open: upper
  _7_Segment_Display u_7_segment_display_19 (
    .D(divider_9_rem[3]), .C(divider_9_rem[2]), .B(divider_9_rem[1]), .A(divider_9_rem[0]),
    .a_2(n7_segment_display_19_a_2), .b_2(n7_segment_display_19_b_2), .c_2(n7_segment_display_19_c_2),
    .d_2(n7_segment_display_19_d_2), .e(n7_segment_display_19_e), .f(n7_segment_display_19_f),
    .g(n7_segment_display_19_g));
  _7_Segment_Display_part u_7_segment_display_20 (
    .g(n7_segment_display_19_g), .f(n7_segment_display_19_f), .a(n7_segment_display_19_a_2),
    .b(n7_segment_display_19_b_2), .e(n7_segment_display_19_e), .d(n7_segment_display_19_d_2),
    .c(n7_segment_display_19_c_2));  // open: dp

  // Notes on the sheet:
  //   Transfer
  //   Complement
  //   Subtract
  //   Multiply
  //   Or
  //   And
  //   Add
  //   Divide
  //   The double buffer is used to avoid race condition.
  //   The Error is only for division by zero (Arithmetic Error).
endmodule

module ALU (
  input  [15:0] a,
  input  [2:0] c,
  input  [15:0] b,
  output [31:0] Output,
  output Error
);

  wire and_3_out, xor_1_out;
  wire [15:0] adder_1_out, adder_3_out, adder_6_out, and_2_out, divider_1_out, multiplexer_1_out,
       multiplexer_2_out, multiplexer_3_out, multiplexer_4_out, multiplexer_5_out, multiplexer_6_out,
       multiplexer_6_out_2, multiplier_1_cout, multiplier_1_out, not_2_out, not_4_out, not_5_out, not_7_out,
       or_1_out, or_3_out;
  wire [15:15] and_1_out, or_2_out, xor_2_out;
  wire [31:0] adder_2_out, adder_4_out, adder_5_out, adder_7_out, not_1_out, not_3_out, not_6_out;

  // Probe on a
  assign not_1_out = ~{{17{a[15]}}, a[14:0]};  // NOT_Gate not_1, 32 bits wide
  // Probe on b
  assign or_1_out = b | {16{1'b0}};  // OR_Gate or_1, 16 bits wide
  assign not_2_out = ~b;  // NOT_Gate not_2, 16 bits wide
  Adder #(.width(16)) adder_1 (.a(not_2_out), .b(16'h1), .out(adder_1_out));  // open: cin, cout
  assign not_3_out = ~{multiplier_1_cout, multiplier_1_out};  // NOT_Gate not_3, 32 bits wide
  xor xor_1 (xor_1_out, a[15], b[15]);
  assign not_4_out = ~divider_1_out;  // NOT_Gate not_4, 16 bits wide
  xor xor_2 (xor_2_out[15], a[15], b[15]);
  assign not_5_out = ~or_1_out;  // NOT_Gate not_5, 16 bits wide
  or or_2 (or_2_out[15], a[15], b[15]);
  and and_1 (and_1_out[15], a[15], b[15]);
  assign not_6_out = ~{{17{b[15]}}, b[14:0]};  // NOT_Gate not_6, 32 bits wide
  Multiplexer #(.width(16)) multiplexer_1 (
    .in0(b), .in1(adder_1_out), .out(multiplexer_1_out), .sel(b[15]));  // open: en
  Adder #(.width(32)) adder_2 (.a(not_3_out), .b(32'h1), .out(adder_2_out));  // open: cin, cout
  Adder #(.width(16)) adder_3 (.a(not_4_out), .b(16'h1), .out(adder_3_out));  // open: cin, cout
  assign or_3_out = a | b;  // OR_Gate or_3, 16 bits wide
  assign and_2_out = a & b;  // AND_Gate and_2, 16 bits wide
  Adder #(.width(32)) adder_4 (.a(not_6_out), .b(32'h1), .out(adder_4_out));  // open: cin, cout
  assign not_7_out = ~a;  // NOT_Gate not_7, 16 bits wide
  Multiplexer #(.width(16)) multiplexer_2 (
    .in0(multiplier_1_out), .in1(adder_2_out[15:0]), .out(multiplexer_2_out), .sel(xor_1_out));  // open: en
  Multiplexer #(.width(16)) multiplexer_3 (
    .in0(multiplier_1_cout), .in1(adder_2_out[31:16]), .out(multiplexer_3_out), .sel(xor_1_out));  // open: en
  Multiplexer #(.width(16)) multiplexer_4 (
    .in0(divider_1_out), .in1(adder_3_out), .out(multiplexer_4_out), .sel(xor_2_out[15]));  // open: en
  Adder #(.width(32)) adder_5 (.a({{17{a[15]}}, a[14:0]}), .b(adder_4_out), .out(adder_5_out));  // open: cin, cout
  Adder #(.width(16)) adder_6 (.a(not_7_out), .b(16'h1), .out(adder_6_out));  // open: cin, cout
  and and_3 (and_3_out, not_5_out[0], not_5_out[1], not_5_out[2], not_5_out[3], not_5_out[4], not_5_out[5], not_5_out[6], not_5_out[7], not_5_out[8], not_5_out[9], not_5_out[10], not_5_out[11], not_5_out[12], not_5_out[13], not_5_out[14], not_5_out[15]);
  Multiplexer #(.width(16)) multiplexer_5 (
    .in0(a), .in1(adder_6_out), .out(multiplexer_5_out), .sel(a[15]));  // open: en
  Adder #(.width(32)) adder_7 (
    .a({{17{a[15]}}, a[14:0]}), .b({{17{b[15]}}, b[14:0]}), .out(adder_7_out));  // open: cin, cout
  Multiplier #(.width(16)) multiplier_1 (
    .a(multiplexer_5_out), .b(multiplexer_1_out), .out(multiplier_1_out), .cout(multiplier_1_cout));  // open: cin
  Divider #(.width(16)) divider_1 (
    .a(multiplexer_5_out), .b(multiplexer_1_out), .out(divider_1_out));  // open: upper, rem
  Multiplexer #(.width(32)) multiplexer_6 (
    .in0({{16{xor_2_out[15]}}, multiplexer_4_out}), .in1({32{1'b1}}),
    .out({multiplexer_6_out_2, multiplexer_6_out}), .sel(and_3_out));  // open: en
  Multiplexer #(.select(3), .enable("false")) multiplexer_7 (
    .in0(1'b0), .in1(1'b0), .in2(1'b0), .in3(1'b0), .in4(1'b0), .in5(1'b0), .in6(1'b0), .in7(and_3_out),
    .out(Error), .sel(c));
  Multiplexer #(.select(3), .width(16), .enable("false")) multiplexer_8 (
    .in0(a), .in1(or_3_out), .in2(and_2_out), .in3(not_1_out[15:0]), .in4(adder_7_out[15:0]),
    .in5(adder_5_out[15:0]), .in6(multiplexer_2_out), .in7(multiplexer_6_out), .out(Output[15:0]), .sel(c));
  Multiplexer #(.select(3), .width(16), .enable("false")) multiplexer_9 (
    .in0({16{a[15]}}), .in1({16{or_2_out[15]}}), .in2({16{and_1_out[15]}}), .in3(not_1_out[31:16]),
    .in4(adder_7_out[31:16]), .in5(adder_5_out[31:16]), .in6(multiplexer_3_out), .in7(multiplexer_6_out_2),
    .out(Output[31:16]), .sel(c));
  // Probe on Output

  // Notes on the sheet:
  //   5)ADD :- In this we have simply add the numbers. 
  //   6)SUBTRACTION :- In this we have taken the 2's complement of B and then added with A.
  //   4)COMPLEMENT :- Taken the whole complement and then transfer the least 16 bits to A and most 16 bits to B.
  //   1)Transfer :- In transfer we have passed least 16 bits as A and the most 16 bits as the sign bit of A. And then finally merge and answer came. 
  //   2)OR,AND :- In A MUX we have passed the OR of both the numbers and for most 16 bits we have passed the sign bits whether if A or B is negative then the most 16 bits would be 1.
  //   Multiplication
  //   Division
  //   Garbage Value
  //   7) MULTIPLICATION :- In this we have first taken the 2's complement of both number if they are negative and then multipy thier 16 bits using multiplier and then for final answer if any one of the two given number is negative then again taken the 2's complment of entire answer and then splitted it in two parts and provided as input to MUX A and B.
  //   8) DIVISION :- In this we have first taken the 2's complement of both number if they are negative and then divide thier 16 bits using division and then checked if any one is negative then feed the most 16 bits with 1 and least with either their 2's complement if anyone is negative or with just answer.Then for error portion we have taken the logical OR of B's 32 bits with 0 and if all are zero then B is zero then we have taken it's complement and checked if all are zero then error is there and for it we have used MUX where first 6th cases are zero beacuse in it there is no chance of error and if division is there then there is chance of error.
endmodule

module _7_Segment_Display (
  input  D,
  input  C,
  input  B,
  input  A,
  output a_2,
  output b_2,
  output c_2,
  output d_2,
  output e,
  output f,
  output g
);

  wire and_1_out, and_2_out, and_3_out, and_4_out, and_5_out, and_6_out, and_7_out, and_8_out, and_9_out,
       and_10_out, and_11_out, and_12_out, and_13_out, and_14_out, and_15_out, and_16_out, not_1_out,
       not_2_out, not_3_out, not_4_out, not_5_out, not_6_out, not_7_out, not_8_out, not_9_out, not_10_out,
       not_11_out, not_12_out, not_13_out, not_14_out, not_15_out, not_16_out, not_17_out, not_18_out,
       not_19_out, not_20_out, not_21_out;

  not not_1 (not_1_out, C);
  and and_1 (and_1_out, not_1_out, not_2_out);
  not not_2 (not_2_out, A);
  and and_2 (and_2_out, C, A);
  not not_3 (not_3_out, C);
  not not_4 (not_4_out, B);
  and and_3 (and_3_out, not_4_out, not_5_out);
  not not_5 (not_5_out, A);
  and and_4 (and_4_out, B, A);
  not not_6 (not_6_out, B);
  or or_1 (c_2, not_6_out, A, C);
  not not_7 (not_7_out, C);
  and and_5 (and_5_out, not_7_out, not_8_out);
  not not_8 (not_8_out, A);
  not not_9 (not_9_out, C);
  and and_6 (and_6_out, not_9_out, B);
  and and_7 (and_7_out, B, not_10_out);
  not not_10 (not_10_out, A);
  not not_11 (not_11_out, B);
  and and_8 (and_8_out, C, not_11_out, A);
  not not_12 (not_12_out, C);
  and and_9 (and_9_out, not_12_out, not_13_out);
  not not_13 (not_13_out, A);
  and and_10 (and_10_out, B, not_14_out);
  not not_14 (not_14_out, A);
  not not_15 (not_15_out, B);
  and and_11 (and_11_out, not_15_out, not_16_out);
  not not_16 (not_16_out, A);
  and and_12 (and_12_out, C, not_17_out);
  not not_17 (not_17_out, B);
  and and_13 (and_13_out, C, not_18_out);
  not not_18 (not_18_out, A);
  not not_19 (not_19_out, C);
  and and_14 (and_14_out, not_19_out, B);
  and and_15 (and_15_out, C, not_20_out);
  not not_20 (not_20_out, B);
  and and_16 (and_16_out, C, not_21_out);
  not not_21 (not_21_out, A);
  or or_2 (a_2, and_1_out, B, and_2_out, D);
  or or_3 (b_2, not_3_out, and_3_out, and_4_out);
  or or_4 (d_2, and_5_out, and_6_out, and_7_out, and_8_out, D);
  or or_5 (e, and_9_out, and_10_out);
  or or_6 (f, and_11_out, and_12_out, and_13_out, D);
  or or_7 (g, and_14_out, and_15_out, and_16_out, D);
endmodule
